// Logisim project miniCurso.circ as structural Verilog: 9 circuits, main circuit main
module main (
  input  A,
  input  B,
  input  carry_in,
  input  in_4,
  input  in_5,
  input  in_6,
  input  A_2,
  input  B_2,
  output carry_out,
  output Soma_Final,
  output carry_out_2,
  output Soma_Final_2,
  output Cin,
  output SomaAB
);

  wire halfadder_1_carry_in, halfadder_1_somaab, halfadder_2_carry_in;

  FullAdder fulladder_1 (.A(in_4), .B(in_5), .carry_in(in_6), .carry_out_final(carry_out_2), .S(Soma_Final_2));
  HalfAdder halfadder_1 (.A(A), .B(B), .carry_in(halfadder_1_carry_in), .SomaAB(halfadder_1_somaab));
  FullAdder fulladder_2 ();  // open: A, B, carry_in, carry_out_final, S
  HalfAdder halfadder_2 (.A(halfadder_1_somaab), .B(carry_in), .carry_in(halfadder_2_carry_in), .SomaAB(Soma_Final));
  or or_1 (carry_out, halfadder_1_carry_in, halfadder_2_carry_in);
  and and_1 (Cin, A_2, B_2);
  xor xor_1 (SomaAB, A_2, B_2);
endmodule

module HalfAdder (
  input  A,
  input  B,
  output carry_in,
  output SomaAB
);

  and and_1 (carry_in, A, B);
  xor xor_1 (SomaAB, A, B);
endmodule

module FullAdder (
  input  A,
  input  B,
  input  carry_in,
  output carry_out_final,
  output S
);

  wire and_1_out, and_2_out, xor_1_out;

  and and_1 (and_1_out, A, B);
  xor xor_1 (xor_1_out, A, B);
  xor xor_2 (S, xor_1_out, carry_in);
  and and_2 (and_2_out, xor_1_out, carry_in);
  or or_1 (carry_out_final, and_1_out, and_2_out);

  // Notes on the sheet:
  //   carry out1
  //   S1
  //                     carry out2
endmodule

module FullAdderWithTwoHalfAdder (
  input  A,
  input  B,
  input  carry_in,
  output carry_out,
  output Soma_Final
);

  wire halfadder_1_carry_in, halfadder_1_somaab, halfadder_2_carry_in;

  HalfAdder halfadder_1 (.A(A), .B(B), .carry_in(halfadder_1_carry_in), .SomaAB(halfadder_1_somaab));
  HalfAdder halfadder_2 (.A(halfadder_1_somaab), .B(carry_in), .carry_in(halfadder_2_carry_in), .SomaAB(Soma_Final));
  or or_1 (carry_out, halfadder_1_carry_in, halfadder_2_carry_in);
endmodule

module RippleCarryAdder (
  input  [7:0] A,
  input  in_2,
  input  [7:0] B,
  input  in_4,
  input  in_5,
  input  in_6,
  input  in_7,
  input  in_8,
  input  in_9,
  input  in_10,
  input  in_11,
  input  in_12,
  input  in_13,
  input  in_14,
  input  in_15,
  input  in_16,
  input  in_17,
  input  in_18,
  input  in_19,
  input  in_20,
  output out_21,
  output [7:0] Resultado_Soma,
  output out_23,
  output out_24,
  output out_25,
  output out_26,
  output out_27,
  output out_28,
  output out_29,
  output out_30,
  output out_31
);

  wire fulladder_2_carry_out_final, fulladder_3_carry_out_final, fulladder_4_carry_out_final,
       fulladder_5_carry_out_final, fulladder_6_carry_out_final, fulladder_7_carry_out_final,
       fulladder_8_carry_out_final, fulladder_9_carry_out_final, fulladder_10_carry_out_final,
       fulladder_11_carry_out_final, fulladder_12_carry_out_final, fulladder_13_carry_out_final,
       fulladder_14_carry_out_final, fulladder_15_carry_out_final;

  FullAdder fulladder_1 (
    .A(A[7]), .B(B[7]), .carry_in(fulladder_3_carry_out_final), .carry_out_final(out_21),
    .S(Resultado_Soma[7]));
  FullAdder fulladder_2 (
    .A(in_5), .B(in_6), .carry_in(in_4), .carry_out_final(fulladder_2_carry_out_final), .S(out_23));
  FullAdder fulladder_3 (
    .A(A[6]), .B(B[6]), .carry_in(fulladder_6_carry_out_final),
    .carry_out_final(fulladder_3_carry_out_final), .S(Resultado_Soma[6]));
  FullAdder fulladder_4 (
    .A(in_7), .B(in_8), .carry_in(fulladder_2_carry_out_final),
    .carry_out_final(fulladder_4_carry_out_final), .S(out_24));
  FullAdder fulladder_5 (
    .A(A[4]), .B(B[4]), .carry_in(fulladder_8_carry_out_final),
    .carry_out_final(fulladder_5_carry_out_final), .S(Resultado_Soma[4]));
  FullAdder fulladder_6 (
    .A(A[5]), .B(B[5]), .carry_in(fulladder_5_carry_out_final),
    .carry_out_final(fulladder_6_carry_out_final), .S(Resultado_Soma[5]));
  FullAdder fulladder_7 (
    .A(in_9), .B(in_10), .carry_in(fulladder_4_carry_out_final),
    .carry_out_final(fulladder_7_carry_out_final), .S(out_25));
  FullAdder fulladder_8 (
    .A(A[3]), .B(B[3]), .carry_in(fulladder_10_carry_out_final),
    .carry_out_final(fulladder_8_carry_out_final), .S(Resultado_Soma[3]));
  FullAdder fulladder_9 (
    .A(in_11), .B(in_12), .carry_in(fulladder_7_carry_out_final),
    .carry_out_final(fulladder_9_carry_out_final), .S(out_26));
  FullAdder fulladder_10 (
    .A(A[2]), .B(B[2]), .carry_in(fulladder_12_carry_out_final),
    .carry_out_final(fulladder_10_carry_out_final), .S(Resultado_Soma[2]));
  FullAdder fulladder_11 (
    .A(in_13), .B(in_14), .carry_in(fulladder_9_carry_out_final),
    .carry_out_final(fulladder_11_carry_out_final), .S(out_27));
  FullAdder fulladder_12 (
    .A(A[1]), .B(B[1]), .carry_in(fulladder_14_carry_out_final),
    .carry_out_final(fulladder_12_carry_out_final), .S(Resultado_Soma[1]));
  FullAdder fulladder_13 (
    .A(in_15), .B(in_16), .carry_in(fulladder_11_carry_out_final),
    .carry_out_final(fulladder_13_carry_out_final), .S(out_28));
  FullAdder fulladder_14 (
    .A(A[0]), .B(B[0]), .carry_in(in_2), .carry_out_final(fulladder_14_carry_out_final), .S(Resultado_Soma[0]));
  FullAdder fulladder_15 (
    .A(in_17), .B(in_18), .carry_in(fulladder_13_carry_out_final),
    .carry_out_final(fulladder_15_carry_out_final), .S(out_29));
  FullAdder fulladder_16 (
    .A(in_19), .B(in_20), .carry_in(fulladder_15_carry_out_final), .carry_out_final(out_31), .S(out_30));
endmodule

module FlipFlopRSNand (
  input  A,
  input  B,
  output Q,
  output nQ
);

  nand nand_1 (Q, ~A, nQ);  // NAND_Gate
  nand nand_2 (nQ, Q, ~B);  // NAND_Gate
endmodule

module FlipFlopRSNandWithClock (
  input  S,
  input  R,
  output out_3,
  output out_4
);

  wire Clock_out, nand_1_out, nand_2_out;

  Clock Clock (.out(Clock_out));
  nand nand_1 (nand_1_out, S, Clock_out);
  nand nand_2 (nand_2_out, Clock_out, R);
  nand nand_3 (out_3, nand_1_out, out_4);
  nand nand_4 (out_4, out_3, nand_2_out);
endmodule

module FlipFlopSRNor (
  input  A,
  input  B,
  output Q,
  output nQ
);

  nor nor_1 (Q, A, nQ);
  nor nor_2 (nQ, Q, B);
endmodule

module FlipFlopJK (
  input  in_1,
  input  in_2,
  output out_3,
  output out_4
);

  wire clock_1_out;

  Clock clock_1 (.out(clock_1_out));
  J_K_Flip_Flop j_k_ff_1 (.J(in_1), .clk(clock_1_out), .K(in_2), .Q(out_3), .Qn(out_4));  // open: preset, en, reset

  // Notes on the sheet:
  //                                                                                                           Infelizmente por causa das limitacões do logisim não foi possível implementar igual aos outros circutos
endmodule
